# Fritzing sketch GDO_ESP32_c3 on mini breadboard (saved by Fritzing 1.0.5)
breadboards: 1

parts:
  A2 = Esp32-c3 super mini
  A3401 = MOSFET-NCHANNEL [package=sot23-3]  # not connected
  2n7000 = MOSFET-NCHANNEL [package=to-92]
  R8 = Resistor upright [tolerance=±5% resistance=1k package=THT]
  R9 = Resistor upright [tolerance=±5% resistance=10k package=THT]
  R10 = Resistor [tolerance=±5% power=0.25W resistance=10k package=THT]
  R11 = Resistor [tolerance=±5% power=0.25W resistance=10k package=THT]
  A3400 = IC, SIP package, 3 pins [chip_label=A3400]

nets:
  N1: A2.Pin_7, 2n7000.D
  N2: A2.Pin_8, R8.Pin_0, R10.Pin_0
  Chamberlain 2 (white/ground): A2.Pin_15, 2n7000.S, R9.Pin_1, A3400.pin1
  N3: 2n7000.G, R10.Pin_1, R11.Pin_1
  N4: R8.Pin_1, A3400.pin3
  Chamberlain 0 (green/signal port): R9.Pin_0, R11.Pin_0, A3400.pin2

notes:
  GND (white slot 2 on chamberlain)
  Signal (green slot 0 on chamberlain)
  also consider: https://github.com/konnected-io/konnected-esphome/tree/master/components/secplus_gdo
  based on: https://github.com/GelidusResearch/esphome-secplus-gdo?tab=readme-ov-file

custom parts:
  Esp32-c3 super mini: ESP32-C3 Development Board ESP32 SuperMini Development Board ESP32 Development Board WiFi Bluetooth.
  MOSFET-NCHANNEL: Generic NMOS footprint
  Resistor upright: A generic upright standing resistor (0.25W)
